# Fritzing sketch LargeDigits standalone digital buttons (saved by Fritzing 0.9.4)
breadboards: 1

parts:
  PART1 = SparkFun Large Digit Driver [part_number=WIG-13279]
  PART2 = SparkFun Large Digit Driver [part_number=WIG-13279]
  SparkFun_RedBoard_Qwiic1 = SparkFun RedBoard Qwiic
  S1 = Pushbutton [package="[THT]"]
  S2 = Pushbutton [package="[THT]"]
  R1 = Resistor [tolerance=±5% resistance=10k package="0402 [SMD]"]
  R2 = Resistor [tolerance=±5% resistance=10k package="0402 [SMD]"]

nets:
  N1: PART1.GND, PART2.GND#0
  N2: PART1.LAT, PART2.LAT#1
  N3: PART1.CLK, PART2.CLK#2
  N4: PART1.SER, PART2.SER#3
  N5: PART1.5V, PART2.5V#4
  N6: PART1.12V, PART2.12V#5
  N7: PART2.GND#6, SparkFun_RedBoard_Qwiic1.GND, R1.Pin_1, R2.Pin_0
  N8: PART2.LAT#7, SparkFun_RedBoard_Qwiic1.D5_PWM
  N9: PART2.CLK#8, SparkFun_RedBoard_Qwiic1.D6_PWM
  N10: PART2.SER#9, SparkFun_RedBoard_Qwiic1.D7
  N11: PART2.5V#10, SparkFun_RedBoard_Qwiic1.5V, SparkFun_RedBoard_Qwiic1.IOREF
  N12: PART2.12V#11, SparkFun_RedBoard_Qwiic1.VIN
  N13: SparkFun_RedBoard_Qwiic1.3.3V, S1.Pin_3, S1.Pin_4, S2.Pin_3, S2.Pin_4, R1.Pin_0, R2.Pin_1
  N14: SparkFun_RedBoard_Qwiic1.D2, S1.Pin_1, S1.Pin_2
  N15: SparkFun_RedBoard_Qwiic1.D3_PWM, S2.Pin_1, S2.Pin_2

notes:
  The GND pin from the Arduino is connected to the bottom row of the breadboard, the 3.3V pin from the Arduino to the top row. There is a 10k ohm resister between the gnd row and the button, and the button outputs are connected to pins 2 and 3 of the Arduino.

custom parts:
  SparkFun Large Digit Driver: Driver board for the large 7-Segment Display - 6.5" at SparkFun. For specs and online guides, please visit: www.sparkfun.com/products/13279
  SparkFun RedBoard Qwiic: At SparkFun we continually like to innovate, update, and improve even when it comes to our very own development boards. We have multiple versions of the SparkFun RedBoard in our catalog but none of them in an R3 form factor with a Qwiic connector on it to make I2C easy... until now! The SparkFun RedBoard Qwiic is an Arduino-compatible development board that uses a few of the features that we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
