# Fritzing sketch LargeDigits with Microbit Serial Interface (saved by Fritzing 0.9.4)

parts:
  Mod1 = Microbit
  PART1 = SparkFun Large Digit Driver [part_number=WIG-13279]
  PART2 = SparkFun Large Digit Driver [part_number=WIG-13279]
  SparkFun_RedBoard_Qwiic1 = SparkFun RedBoard Qwiic

nets:
  N1: Mod1.P0, SparkFun_RedBoard_Qwiic1.D2
  N2: Mod1.P1, SparkFun_RedBoard_Qwiic1.D3_PWM
  3V3: Mod1.3V3, SparkFun_RedBoard_Qwiic1.3.3V
  GND: Mod1.GND, PART2.GND#6, SparkFun_RedBoard_Qwiic1.GND
  N3: PART1.GND, PART2.GND#0
  N4: PART1.LAT, PART2.LAT#1
  N5: PART1.CLK, PART2.CLK#2
  N6: PART1.SER, PART2.SER#3
  N7: PART1.5V, PART2.5V#4
  N8: PART1.12V, PART2.12V#5
  N9: PART2.LAT#7, SparkFun_RedBoard_Qwiic1.D5_PWM
  N10: PART2.CLK#8, SparkFun_RedBoard_Qwiic1.D6_PWM
  N11: PART2.SER#9, SparkFun_RedBoard_Qwiic1.D7
  N12: PART2.5V#10, SparkFun_RedBoard_Qwiic1.5V, SparkFun_RedBoard_Qwiic1.IOREF
  N13: PART2.12V#11, SparkFun_RedBoard_Qwiic1.VIN

custom parts:
  Microbit: BBC Microbit Fritzing part. May 2019 expanded to include schematic and pcb views as well as breadboard. PCB view assumes an Adafruit PRODUCT ID: 3342 2x40 Right Angle through hole edge connector (although others will probably work as well). The pcb svg is custom (see forum article http://forum.fritzing.org/t/making-edge-connectors-and-both-side-smd-parts/7287 for an explaination if you need to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
  SparkFun Large Digit Driver: Driver board for the large 7-Segment Display - 6.5" at SparkFun. For specs and online guides, please visit: www.sparkfun.com/products/13279
  SparkFun RedBoard Qwiic: At SparkFun we continually like to innovate, update, and improve even when it comes to our very own development boards. We have multiple versions of the SparkFun RedBoard in our catalog but none of them in an R3 form factor with a Qwiic connector on it to make I2C easy... until now! The SparkFun RedBoard Qwiic is an Arduino-compatible development board that uses a few of the features that we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
