# Fritzing sketch LargeDigits with wireless nrf24l01 (saved by Fritzing 0.9.4)

parts:
  PART1 = SparkFun Large Digit Driver [part_number=WIG-13279]
  PART2 = SparkFun Large Digit Driver [part_number=WIG-13279]
  SparkFun_RedBoard_Qwiic1 = SparkFun RedBoard Qwiic
  Part1 = NRF24L01+ Breakout Board

nets:
  N1: PART1.GND, PART2.GND#0
  N2: PART1.LAT, PART2.LAT#1
  N3: PART1.CLK, PART2.CLK#2
  N4: PART1.SER, PART2.SER#3
  N5: PART1.5V, PART2.5V#4
  N6: PART1.12V, PART2.12V#5
  GND: PART2.GND#6, SparkFun_RedBoard_Qwiic1.GND, Part1.GND
  N7: PART2.LAT#7, SparkFun_RedBoard_Qwiic1.D5_PWM
  N8: PART2.CLK#8, SparkFun_RedBoard_Qwiic1.D6_PWM
  N9: PART2.SER#9, SparkFun_RedBoard_Qwiic1.D7
  N10: PART2.5V#10, SparkFun_RedBoard_Qwiic1.5V, SparkFun_RedBoard_Qwiic1.IOREF
  N11: PART2.12V#11, SparkFun_RedBoard_Qwiic1.VIN
  N12: SparkFun_RedBoard_Qwiic1.D13/SCK, Part1.SCK
  N13: SparkFun_RedBoard_Qwiic1.D12/MISO, Part1.MISO
  N14: SparkFun_RedBoard_Qwiic1.D11_PWM/MOSI, Part1.MOSI
  N15: SparkFun_RedBoard_Qwiic1.D10_PWM/SS, Part1.CS
  N16: SparkFun_RedBoard_Qwiic1.D9_PWM, Part1.CE
  3.3V: SparkFun_RedBoard_Qwiic1.3.3V, Part1.VCC

custom parts:
  SparkFun Large Digit Driver: Driver board for the large 7-Segment Display - 6.5" at SparkFun. For specs and online guides, please visit: www.sparkfun.com/products/13279
  SparkFun RedBoard Qwiic: At SparkFun we continually like to innovate, update, and improve even when it comes to our very own development boards. We have multiple versions of the SparkFun RedBoard in our catalog but none of them in an R3 form factor with a Qwiic connector on it to make I2C easy... until now! The SparkFun RedBoard Qwiic is an Arduino-compatible development board that uses a few of the features that we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
